// Logisim project my_compuer.circ as structural Verilog: 33 circuits, main circuit And
module And (
  input  a,
  input  b,
  output out_3
);

  wire nand_1_out;

  nand nand_1 (nand_1_out, a, b);
  nand nand_2 (out_3, nand_1_out, nand_1_out);
endmodule

module Not (
  input  in_1,
  output out_2
);

  nand nand_1 (out_2, in_1, in_1);
endmodule

module Or (
  input  in_1,
  input  in_2,
  output out_3
);

  wire not_1_out_2, not_2_out_2;

  Not not_1 (.in_1(in_1), .out_2(not_1_out_2));
  Not not_2 (.in_1(in_2), .out_2(not_2_out_2));
  nand nand_1 (out_3, not_1_out_2, not_2_out_2);
endmodule

module Xor (
  input  a,
  input  b,
  output out_3
);

  wire and_1_out_3, not_1_out_2, or_1_out_3;

  And and_1 (.a(a), .b(b), .out_3(and_1_out_3));
  Or or_1 (.in_1(a), .in_2(b), .out_3(or_1_out_3));
  Not not_1 (.in_1(and_1_out_3), .out_2(not_1_out_2));
  And and_2 (.a(not_1_out_2), .b(or_1_out_3), .out_3(out_3));
endmodule

module Mux (
  input  a,
  input  b,
  input  sel,
  output out_4
);

  wire and_1_out_3, and_2_out_3, not_1_out;

  not not_1 (not_1_out, sel);
  And and_1 (.a(a), .b(not_1_out), .out_3(and_1_out_3));
  And and_2 (.a(b), .b(sel), .out_3(and_2_out_3));
  Or or_1 (.in_1(and_1_out_3), .in_2(and_2_out_3), .out_3(out_4));
endmodule

module Main (
  input  in_1,
  input  in_2,
  input  in_3,
  input  in_4,
  input  in_5,
  input  in_6,
  input  [7:0] store_data,
  input  store,
  input  in_9,
  input  [7:0] address,
  input  in_11,
  input  clock,
  input  [7:0] in_13,
  input  in_14,
  output out_15,
  output out_16,
  output out_17,
  output out_18,
  output out_19,
  output out_20,
  output out_21,
  output out_22,
  output out_23,
  output [7:0] load_store_data,
  output [7:0] out_25
);

  wire clock_1_out, not_1_out;

  Clock clock_1 (.out(clock_1_out));
  D_Flip_Flop d_ff_1 (.clk(clock_1_out), .D(in_3), .Q(out_15), .Qn(out_17));  // open: preset, en, reset
  T_Flip_Flop t_ff_1 (.clk(clock_1_out), .T(in_4), .Q(out_18), .Qn(out_19));  // open: preset, reset, en
  J_K_Flip_Flop j_k_ff_1 (.J(in_5), .clk(clock_1_out), .K(in_6), .Q(out_20), .Qn(out_21));  // open: preset, en, reset
  S_R_Flip_Flop s_r_ff_1 (.S(in_9), .clk(clock_1_out), .R(in_11), .Q(out_22), .Qn(out_23));  // open: preset, reset, en
  Register register_1 (.D(in_13), .Q(out_25), .clk(in_14));  // open: en, clr
  Bit bit_1 (.i(in_2), .s(in_1), .out_3(out_16));
  assign load_store_data = store ? store_data : 8'bz;  // Controlled_Buffer controlled_buffer_1
  not not_1 (not_1_out, store);
  RAM ram_1 (.addr(address), .data(load_store_data), .clk(clock), .ld(not_1_out));  // open: sel, clr
endmodule

module DMux (
  input  in,
  input  sel,
  output a,
  output b
);

  wire not_1_out_2;

  Not not_1 (.in_1(sel), .out_2(not_1_out_2));
  And and_1 (.a(in), .b(not_1_out_2), .out_3(a));
  And and_2 (.a(in), .b(sel), .out_3(b));
endmodule

module Not16 (
  input  [15:0] in_1,
  output [15:0] out_2
);

  Not not_1 (.out_2(out_2[0]));  // open: in_1
  Not not_2 (.out_2(out_2[1]));  // open: in_1
  Not not_3 (.in_1(in_1[2]), .out_2(out_2[2]));
  Not not_4 (.in_1(in_1[3]), .out_2(out_2[3]));
  Not not_5 (.in_1(in_1[4]), .out_2(out_2[4]));
  Not not_6 (.in_1(in_1[5]), .out_2(out_2[5]));
  Not not_7 (.in_1(in_1[6]), .out_2(out_2[6]));
  Not not_8 (.in_1(in_1[7]), .out_2(out_2[7]));
  Not not_9 (.in_1(in_1[8]), .out_2(out_2[8]));
  Not not_10 (.in_1(in_1[9]), .out_2(out_2[9]));
  Not not_11 (.in_1(in_1[10]), .out_2(out_2[10]));
  Not not_12 (.in_1(in_1[11]), .out_2(out_2[11]));
  Not not_13 (.in_1(in_1[12]), .out_2(out_2[12]));
  Not not_14 (.in_1(in_1[13]), .out_2(out_2[13]));
  Not not_15 (.in_1(in_1[14]), .out_2(out_2[14]));
  Not not_16 (.in_1(in_1[15]), .out_2(out_2[15]));
endmodule

module And16 (
  input  [15:0] in_1,
  input  [15:0] in_2,
  output [15:0] out_3
);

  And and_1 (.a(in_1[0]), .b(in_2[0]), .out_3(out_3[0]));
  And and_2 (.a(in_1[1]), .b(in_2[1]), .out_3(out_3[1]));
  And and_3 (.a(in_1[2]), .b(in_2[2]), .out_3(out_3[2]));
  And and_4 (.a(in_1[3]), .b(in_2[3]), .out_3(out_3[3]));
  And and_5 (.a(in_1[4]), .b(in_2[4]), .out_3(out_3[4]));
  And and_6 (.a(in_1[5]), .b(in_2[5]), .out_3(out_3[5]));
  And and_7 (.a(in_1[6]), .b(in_2[6]), .out_3(out_3[6]));
  And and_8 (.a(in_1[7]), .b(in_2[7]), .out_3(out_3[7]));
  And and_9 (.a(in_1[8]), .b(in_2[8]), .out_3(out_3[8]));
  And and_10 (.a(in_1[9]), .b(in_2[9]), .out_3(out_3[9]));
  And and_11 (.a(in_1[10]), .b(in_2[10]), .out_3(out_3[10]));
  And and_12 (.a(in_1[11]), .b(in_2[11]), .out_3(out_3[11]));
  And and_13 (.a(in_1[12]), .b(in_2[12]), .out_3(out_3[12]));
  And and_14 (.a(in_1[13]), .b(in_2[13]), .out_3(out_3[13]));
  And and_15 (.a(in_1[14]), .b(in_2[14]), .out_3(out_3[14]));
  And and_16 (.a(in_1[15]), .b(in_2[15]), .out_3(out_3[15]));
endmodule

module Or16 (
  input  [15:0] in_1,
  input  [15:0] in_2,
  output [15:0] out_3
);

  Or or_1 (.in_1(in_1[0]), .in_2(in_2[0]), .out_3(out_3[0]));
  Or or_2 (.in_1(in_1[1]), .in_2(in_2[1]), .out_3(out_3[1]));
  Or or_3 (.in_1(in_1[2]), .in_2(in_2[2]), .out_3(out_3[2]));
  Or or_4 (.in_1(in_1[3]), .in_2(in_2[3]), .out_3(out_3[3]));
  Or or_5 (.in_1(in_1[4]), .in_2(in_2[4]), .out_3(out_3[4]));
  Or or_6 (.in_1(in_1[5]), .in_2(in_2[5]), .out_3(out_3[5]));
  Or or_7 (.in_1(in_1[6]), .in_2(in_2[6]), .out_3(out_3[6]));
  Or or_8 (.in_1(in_1[7]), .in_2(in_2[7]), .out_3(out_3[7]));
  Or or_9 (.in_1(in_1[8]), .in_2(in_2[8]), .out_3(out_3[8]));
  Or or_10 (.in_1(in_1[9]), .in_2(in_2[9]), .out_3(out_3[9]));
  Or or_11 (.in_1(in_1[10]), .in_2(in_2[10]), .out_3(out_3[10]));
  Or or_12 (.in_1(in_1[11]), .in_2(in_2[11]), .out_3(out_3[11]));
  Or or_13 (.in_1(in_1[12]), .in_2(in_2[12]), .out_3(out_3[12]));
  Or or_14 (.in_1(in_1[13]), .in_2(in_2[13]), .out_3(out_3[13]));
  Or or_15 (.in_1(in_1[14]), .in_2(in_2[14]), .out_3(out_3[14]));
  Or or_16 (.in_1(in_1[15]), .in_2(in_2[15]), .out_3(out_3[15]));
endmodule

module Mux16 (
  input  [15:0] in_1,
  input  [15:0] in_2,
  input  in_3,
  output [15:0] out_4
);

  Mux mux_1 (.a(in_1[0]), .b(in_2[0]), .sel(in_3), .out_4(out_4[0]));
  Mux mux_2 (.a(in_1[1]), .b(in_2[1]), .sel(in_3), .out_4(out_4[1]));
  Mux mux_3 (.a(in_1[2]), .b(in_2[2]), .sel(in_3), .out_4(out_4[2]));
  Mux mux_4 (.a(in_1[3]), .b(in_2[3]), .sel(in_3), .out_4(out_4[3]));
  Mux mux_5 (.a(in_1[4]), .b(in_2[4]), .sel(in_3), .out_4(out_4[4]));
  Mux mux_6 (.a(in_1[5]), .b(in_2[5]), .sel(in_3), .out_4(out_4[5]));
  Mux mux_7 (.a(in_1[6]), .b(in_2[6]), .sel(in_3), .out_4(out_4[6]));
  Mux mux_8 (.a(in_1[7]), .b(in_2[7]), .sel(in_3), .out_4(out_4[7]));
  Mux mux_9 (.a(in_1[8]), .b(in_2[8]), .sel(in_3), .out_4(out_4[8]));
  Mux mux_10 (.a(in_1[9]), .b(in_2[9]), .sel(in_3), .out_4(out_4[9]));
  Mux mux_11 (.a(in_1[10]), .b(in_2[10]), .sel(in_3), .out_4(out_4[10]));
  Mux mux_12 (.a(in_1[11]), .b(in_2[11]), .sel(in_3), .out_4(out_4[11]));
  Mux mux_13 (.a(in_1[12]), .b(in_2[12]), .sel(in_3), .out_4(out_4[12]));
  Mux mux_14 (.a(in_1[13]), .b(in_2[13]), .sel(in_3), .out_4(out_4[13]));
  Mux mux_15 (.a(in_1[14]), .b(in_2[14]), .sel(in_3), .out_4(out_4[14]));
  Mux mux_16 (.a(in_1[15]), .b(in_2[15]), .sel(in_3), .out_4(out_4[15]));
endmodule

module Or8Way (
  input  in_1,
  input  in_2,
  input  in_3,
  input  in_4,
  input  in_5,
  input  in_6,
  input  in_7,
  input  in_8,
  output out_9
);

  wire or_1_out_3, or_2_out_3, or_3_out_3, or_4_out_3, or_5_out_3, or_7_out_3;

  Or or_1 (.in_1(in_1), .in_2(in_2), .out_3(or_1_out_3));
  Or or_2 (.in_1(or_7_out_3), .in_2(in_6), .out_3(or_2_out_3));
  Or or_3 (.in_1(or_2_out_3), .in_2(in_7), .out_3(or_3_out_3));
  Or or_4 (.in_1(or_1_out_3), .in_2(in_3), .out_3(or_4_out_3));
  Or or_5 (.in_1(or_4_out_3), .in_2(in_4), .out_3(or_5_out_3));
  Or or_6 (.in_1(or_3_out_3), .in_2(in_8), .out_3(out_9));
  Or or_7 (.in_1(or_5_out_3), .in_2(in_5), .out_3(or_7_out_3));
endmodule

module Mux4Way16 (
  input  [15:0] in_1,
  input  [15:0] in_2,
  input  [15:0] in_3,
  input  [15:0] in_4,
  input  in_5,
  input  in_6,
  output [15:0] out_7
);

  wire and_1_out_3, not_1_out_2, or_1_out_3, or_2_out_3;
  wire [15:0] mux16_1_out_4, mux16_2_out_4, mux16_3_out_4, mux16_4_out_4, mux16_5_out_4, mux16_6_out_4;

  Or or_1 (.in_1(in_5), .in_2(in_6), .out_3(or_1_out_3));
  Not not_1 (.in_1(in_5), .out_2(not_1_out_2));
  Or or_2 (.in_1(not_1_out_2), .in_2(in_6), .out_3(or_2_out_3));
  Mux16 mux16_1 (.in_1(in_1), .in_2(in_2), .in_3(or_1_out_3), .out_4(mux16_1_out_4));
  Mux16 mux16_2 (.in_1(in_1), .in_2(in_2), .in_3(or_1_out_3), .out_4(mux16_2_out_4));
  Mux16 mux16_3 (.in_1(in_3), .in_2(in_4), .in_3(or_2_out_3), .out_4(mux16_3_out_4));
  Mux16 mux16_4 (.in_1(in_3), .in_2(in_4), .in_3(or_2_out_3), .out_4(mux16_4_out_4));
  Mux16 mux16_5 (.in_1(mux16_1_out_4), .in_2(mux16_2_out_4), .in_3(or_1_out_3), .out_4(mux16_5_out_4));
  Mux16 mux16_6 (.in_1(mux16_3_out_4), .in_2(mux16_4_out_4), .in_3(or_2_out_3), .out_4(mux16_6_out_4));
  And and_1 (.a(or_1_out_3), .b(in_5), .out_3(and_1_out_3));
  Mux16 mux16_7 (.in_1(mux16_5_out_4), .in_2(mux16_6_out_4), .in_3(and_1_out_3), .out_4(out_7));
endmodule

module Mux8Way16 (
  input  [15:0] in_1,
  input  [15:0] in_2,
  input  [15:0] in_3,
  input  [15:0] in_4,
  input  [15:0] in_5,
  input  [15:0] in_6,
  input  [15:0] in_7,
  input  [15:0] in_8,
  input  sel2,
  input  sel1,
  input  sel0,
  output [15:0] out_12
);

  wire [15:0] mux4way16_1_out_7, mux4way16_2_out_7;

  Mux4Way16 mux4way16_1 (
    .in_1(in_1), .in_2(in_2), .in_3(in_3), .in_4(in_4), .in_5(sel1), .in_6(sel0), .out_7(mux4way16_1_out_7));
  Mux4Way16 mux4way16_2 (
    .in_1(in_5), .in_2(in_6), .in_3(in_7), .in_4(in_8), .in_5(sel1), .in_6(sel0), .out_7(mux4way16_2_out_7));
  Mux16 mux16_1 (.in_1(mux4way16_1_out_7), .in_2(mux4way16_2_out_7), .in_3(sel2), .out_4(out_12));

  // Notes on the sheet:
  //   a
  //   b
  //   c
  //   d
  //   e
  //   f
  //   g
  //   h
  //   t1
  //   t2
endmodule

module DMux4Way (
  input  in,
  input  sel_1,
  input  sel_0,
  output a,
  output b,
  output c,
  output d
);

  wire dmux_1_a, dmux_1_b, not_1_out_2, or_1_out_3;

  DMux dmux_1 (.in(in), .sel(sel_1), .a(dmux_1_a), .b(dmux_1_b));
  Not not_1 (.in_1(sel_1), .out_2(not_1_out_2));
  Or or_1 (.in_1(not_1_out_2), .in_2(sel_0), .out_3(or_1_out_3));
  DMux dmux_2 (.in(dmux_1_a), .sel(sel_0), .a(a), .b(b));
  DMux dmux_3 (.in(dmux_1_b), .sel(or_1_out_3), .a(c), .b(d));

  // Notes on the sheet:
  //   t1
  //   t2
  //   notSel1
  //   oro
endmodule

module DMux8way (
  input  in,
  input  sel_2,
  input  sel_1,
  input  sel_0,
  output a,
  output b,
  output c,
  output d,
  output e,
  output f,
  output g,
  output h
);

  wire dmux_1_a, dmux_1_b;

  DMux dmux_1 (.in(in), .sel(sel_2), .a(dmux_1_a), .b(dmux_1_b));
  DMux4Way dmux4way_1 (.in(dmux_1_a), .sel_1(sel_1), .sel_0(sel_0), .a(a), .b(b), .c(c), .d(d));
  DMux4Way dmux4way_2 (.in(dmux_1_b), .sel_1(sel_1), .sel_0(sel_0), .a(e), .b(f), .c(g), .d(h));

  // Notes on the sheet:
  //   t1
  //   t2
endmodule

module Mux4Way16_v1 (
  input  [15:0] in_1,
  input  [15:0] in_2,
  input  [15:0] in_3,
  input  [15:0] in_4,
  input  sel1,
  input  sel0,
  output [15:0] out_7
);

  wire and_1_out_3, or_1_out_3;
  wire [15:0] mux16_1_out_4, mux16_2_out_4;

  Or or_1 (.in_1(sel1), .in_2(sel0), .out_3(or_1_out_3));
  And and_1 (.a(sel1), .b(sel0), .out_3(and_1_out_3));
  Mux16 mux16_1 (.in_1(in_1), .in_2(in_2), .in_3(or_1_out_3), .out_4(mux16_1_out_4));
  Mux16 mux16_2 (.in_1(mux16_1_out_4), .in_2(in_3), .in_3(sel1), .out_4(mux16_2_out_4));
  Mux16 mux16_3 (.in_1(mux16_2_out_4), .in_2(in_4), .in_3(and_1_out_3), .out_4(out_7));

  // Notes on the sheet:
  //   a
  //   b
  //   c
  //   d
endmodule

module Mux8Way16_v1 (
  input  [15:0] in_1,
  input  [15:0] in_2,
  input  [15:0] in_3,
  input  [15:0] in_4,
  input  [15:0] in_5,
  input  [15:0] in_6,
  input  [15:0] in_7,
  input  [15:0] in_8,
  input  in_9,
  input  in_10,
  input  in_11,
  output [15:0] out_12
);

  wire [15:0] mux4way16_v1_1_out_7, mux4way16_v1_2_out_7;

  Mux4Way16_v1 mux4way16_v1_1 (
    .in_1(in_1), .in_2(in_2), .in_3(in_3), .in_4(in_4), .sel1(in_10), .sel0(in_11),
    .out_7(mux4way16_v1_1_out_7));
  Mux16 mux16_1 (.in_1(mux4way16_v1_1_out_7), .in_2(mux4way16_v1_2_out_7), .in_3(in_9), .out_4(out_12));
  Mux4Way16_v1 mux4way16_v1_2 (
    .in_1(in_5), .in_2(in_6), .in_3(in_7), .in_4(in_8), .sel1(in_10), .sel0(in_11),
    .out_7(mux4way16_v1_2_out_7));
endmodule

module HalfAdder (
  input  a,
  input  b,
  output carry,
  output sum
);

  and and_1 (carry, a, b);
  xor xor_1 (sum, a, b);
endmodule

module FullAdder (
  input  in_1,
  input  in_2,
  input  in_3,
  output out_4,
  output out_5
);

  wire halfadder_1_carry, halfadder_1_sum, halfadder_2_carry;

  HalfAdder halfadder_1 (.a(in_1), .b(in_2), .carry(halfadder_1_carry), .sum(halfadder_1_sum));
  HalfAdder halfadder_2 (.a(halfadder_1_sum), .b(in_3), .carry(halfadder_2_carry), .sum(out_5));
  or or_1 (out_4, halfadder_1_carry, halfadder_2_carry);
endmodule

module Add16 (
  input  [15:0] in_1,
  input  [15:0] in_2,
  output out_3,
  output [15:0] out_4
);

  wire fulladder_1_out_4, fulladder_2_out_4, fulladder_3_out_4, fulladder_4_out_4, fulladder_5_out_4,
       fulladder_6_out_4, fulladder_7_out_4, fulladder_8_out_4, fulladder_9_out_4, fulladder_10_out_4,
       fulladder_11_out_4, fulladder_12_out_4, fulladder_13_out_4, fulladder_14_out_4, fulladder_15_out_4,
       not_1_out;

  FullAdder fulladder_1 (.in_1(not_1_out), .in_2(in_1[0]), .in_3(in_2[0]), .out_4(fulladder_1_out_4), .out_5(out_4[0]));
  FullAdder fulladder_2 (
    .in_1(fulladder_1_out_4), .in_2(in_1[1]), .in_3(in_2[1]), .out_4(fulladder_2_out_4), .out_5(out_4[1]));
  FullAdder fulladder_3 (
    .in_1(fulladder_2_out_4), .in_2(in_1[2]), .in_3(in_2[2]), .out_4(fulladder_3_out_4), .out_5(out_4[2]));
  FullAdder fulladder_4 (
    .in_1(fulladder_3_out_4), .in_2(in_1[3]), .in_3(in_2[3]), .out_4(fulladder_4_out_4), .out_5(out_4[3]));
  FullAdder fulladder_5 (
    .in_1(fulladder_4_out_4), .in_2(in_1[4]), .in_3(in_2[4]), .out_4(fulladder_5_out_4), .out_5(out_4[4]));
  FullAdder fulladder_6 (
    .in_1(fulladder_5_out_4), .in_2(in_1[5]), .in_3(in_2[5]), .out_4(fulladder_6_out_4), .out_5(out_4[5]));
  FullAdder fulladder_7 (
    .in_1(fulladder_6_out_4), .in_2(in_1[6]), .in_3(in_2[6]), .out_4(fulladder_7_out_4), .out_5(out_4[6]));
  FullAdder fulladder_8 (
    .in_1(fulladder_7_out_4), .in_2(in_1[7]), .in_3(in_2[7]), .out_4(fulladder_8_out_4), .out_5(out_4[7]));
  FullAdder fulladder_9 (
    .in_1(fulladder_8_out_4), .in_2(in_1[8]), .in_3(in_2[8]), .out_4(fulladder_9_out_4), .out_5(out_4[8]));
  FullAdder fulladder_10 (
    .in_1(fulladder_9_out_4), .in_2(in_1[9]), .in_3(in_2[9]), .out_4(fulladder_10_out_4), .out_5(out_4[9]));
  FullAdder fulladder_11 (
    .in_1(fulladder_10_out_4), .in_2(in_1[10]), .in_3(in_2[10]), .out_4(fulladder_11_out_4), .out_5(out_4[10]));
  FullAdder fulladder_12 (
    .in_1(fulladder_11_out_4), .in_2(in_1[11]), .in_3(in_2[11]), .out_4(fulladder_12_out_4), .out_5(out_4[11]));
  FullAdder fulladder_13 (
    .in_1(fulladder_12_out_4), .in_2(in_1[12]), .in_3(in_2[12]), .out_4(fulladder_13_out_4), .out_5(out_4[12]));
  FullAdder fulladder_14 (
    .in_1(fulladder_13_out_4), .in_2(in_1[13]), .in_3(in_2[13]), .out_4(fulladder_14_out_4), .out_5(out_4[13]));
  FullAdder fulladder_15 (
    .in_1(fulladder_14_out_4), .in_2(in_1[14]), .in_3(in_2[14]), .out_4(fulladder_15_out_4), .out_5(out_4[14]));
  FullAdder fulladder_16 (
    .in_1(fulladder_15_out_4), .in_2(in_1[15]), .in_3(in_2[15]), .out_4(out_3), .out_5(out_4[15]));
  not not_1 (not_1_out, 1'b1);
endmodule

module Inc16 (
  input  [15:0] in_1,
  output [15:0] out_2
);

  wire [15:15] not_1_out;

  not not_1 (not_1_out[15], 1'b1);
  Add16 add16_1 (.in_1(in_1), .in_2({{15{not_1_out[15]}}, 1'b1}), .out_4(out_2));  // open: out_3
endmodule

module ALU (
  input  zx,
  input  nx,
  input  zy,
  input  ny,
  input  f,
  input  no,
  input  [15:0] x,
  input  [15:0] in_8,
  output [15:0] out_9,
  output zr,
  output ng
);

  wire not_1_out, not_2_out, or_1_out, undriven;
  wire [15:0] adder_1_out, and_1_out, and_2_out, and_3_out, bit_extender_1_out, bit_extender_2_out,
       multiplexer_1_out, multiplexer_2_out, multiplexer_3_out, not_3_out, not_4_out, not_5_out;

  not not_1 (not_1_out, zx);
  assign bit_extender_1_out = {{15{not_1_out}}, not_1_out};  // Bit_Extender bit_extender_1
  assign and_1_out = bit_extender_1_out & x;  // AND_Gate and_1, 16 bits wide
  assign and_2_out = bit_extender_2_out & in_8;  // AND_Gate and_2, 16 bits wide
  not not_2 (not_2_out, zy);
  assign bit_extender_2_out = {{15{not_2_out}}, not_2_out};  // Bit_Extender bit_extender_2
  Multiplexer #(.width(16)) multiplexer_1 (
    .in0(and_1_out), .in1(not_3_out), .out(multiplexer_1_out), .sel(nx), .en(undriven));
  assign not_3_out = ~and_1_out;  // NOT_Gate not_3, 16 bits wide
  Multiplexer #(.width(16)) multiplexer_2 (
    .in0(and_2_out), .in1(not_4_out), .out(multiplexer_2_out), .sel(ny));  // open: en
  assign not_4_out = ~and_2_out;  // NOT_Gate not_4, 16 bits wide
  assign and_3_out = multiplexer_1_out & multiplexer_2_out;  // AND_Gate and_3, 16 bits wide
  Multiplexer #(.width(16)) multiplexer_3 (
    .in0(and_3_out), .in1(adder_1_out), .out(multiplexer_3_out), .sel(f));  // open: en
  Adder #(.width(16)) adder_1 (.a(multiplexer_1_out), .b(multiplexer_2_out), .out(adder_1_out));  // open: cin, cout
  Multiplexer #(.width(16)) multiplexer_4 (
    .in0(multiplexer_3_out), .in1(not_5_out), .out({ng, out_9[14:0]}), .sel(no));  // open: en
  assign not_5_out = ~multiplexer_3_out;  // NOT_Gate not_5, 16 bits wide
  not not_6 (zr, or_1_out);
  or or_1 (or_1_out, out_9[0], out_9[1], out_9[2], out_9[3], out_9[4], out_9[5], out_9[6], out_9[7], out_9[8], out_9[9], out_9[10], out_9[11], out_9[12], out_9[13], out_9[14], ng);

  assign out_9[15] = ng;

  // Notes on the sheet:
  //   y
  //   out
endmodule

module Register16 (
  input  [15:0] in_1,
  input  in_2,
  output [15:0] out_3
);

  Bit bit_1 (.i(in_1[0]), .s(in_2), .out_3(out_3[0]));
  Bit bit_2 (.i(in_1[1]), .s(in_2), .out_3(out_3[1]));
  Bit bit_3 (.i(in_1[2]), .s(in_2), .out_3(out_3[2]));
  Bit bit_4 (.i(in_1[3]), .s(in_2), .out_3(out_3[3]));
  Bit bit_5 (.i(in_1[4]), .s(in_2), .out_3(out_3[4]));
  Bit bit_6 (.i(in_1[5]), .s(in_2), .out_3(out_3[5]));
  Bit bit_7 (.i(in_1[6]), .s(in_2), .out_3(out_3[6]));
  Bit bit_8 (.i(in_1[7]), .s(in_2), .out_3(out_3[7]));
  Bit bit_9 (.i(in_1[8]), .s(in_2), .out_3(out_3[8]));
  Bit bit_10 (.i(in_1[9]), .s(in_2), .out_3(out_3[9]));
  Bit bit_11 (.i(in_1[10]), .s(in_2), .out_3(out_3[10]));
  Bit bit_12 (.i(in_1[11]), .s(in_2), .out_3(out_3[11]));
  Bit bit_13 (.i(in_1[12]), .s(in_2), .out_3(out_3[12]));
  Bit bit_14 (.i(in_1[13]), .s(in_2), .out_3(out_3[13]));
  Bit bit_15 (.i(in_1[14]), .s(in_2), .out_3(out_3[14]));
  Bit bit_16 (.i(in_1[15]), .s(in_2), .out_3(out_3[15]));
endmodule

module Bit (
  input  i,
  input  s,
  output out_3
);

  wire _1_out, _2_out, _4_out;

  nand _1 (_1_out, i, s);
  nand _2 (_2_out, _1_out, s);
  nand _3 (out_3, _1_out, _4_out);
  nand _4 (_4_out, out_3, _2_out);
endmodule

module RAM8 (
  input  [15:0] in_1,
  input  [2:0] addr,
  input  set,
  output [15:0] out_4
);

  wire demultiplexer_2_out0, demultiplexer_2_out1, demultiplexer_2_out2, demultiplexer_2_out3,
       demultiplexer_2_out4, demultiplexer_2_out5, demultiplexer_2_out6, demultiplexer_2_out7;
  wire [15:0] demultiplexer_1_out0, demultiplexer_1_out1, demultiplexer_1_out2, demultiplexer_1_out3,
       demultiplexer_1_out4, demultiplexer_1_out5, demultiplexer_1_out6, demultiplexer_1_out7,
       register16_1_out_3, register16_2_out_3, register16_3_out_3, register16_4_out_3, register16_5_out_3,
       register16_6_out_3, register16_7_out_3, register16_8_out_3;

  Demultiplexer #(.select(3), .width(16)) demultiplexer_1 (
    .out0(demultiplexer_1_out0), .out1(demultiplexer_1_out1), .out2(demultiplexer_1_out2),
    .out3(demultiplexer_1_out3), .out4(demultiplexer_1_out4), .out5(demultiplexer_1_out5),
    .out6(demultiplexer_1_out6), .out7(demultiplexer_1_out7), .in(in_1), .sel(addr));  // open: en
  Demultiplexer #(.select(3)) demultiplexer_2 (
    .out0(demultiplexer_2_out0), .out1(demultiplexer_2_out1), .out2(demultiplexer_2_out2),
    .out3(demultiplexer_2_out3), .out4(demultiplexer_2_out4), .out5(demultiplexer_2_out5),
    .out6(demultiplexer_2_out6), .out7(demultiplexer_2_out7), .in(set), .sel(addr));  // open: en
  Register16 register16_1 (.in_1(demultiplexer_1_out0), .in_2(demultiplexer_2_out0), .out_3(register16_1_out_3));
  Register16 register16_2 (.in_1(demultiplexer_1_out1), .in_2(demultiplexer_2_out1), .out_3(register16_2_out_3));
  Register16 register16_3 (.in_1(demultiplexer_1_out2), .in_2(demultiplexer_2_out2), .out_3(register16_3_out_3));
  Register16 register16_4 (.in_1(demultiplexer_1_out3), .in_2(demultiplexer_2_out3), .out_3(register16_4_out_3));
  Register16 register16_5 (.in_1(demultiplexer_1_out4), .in_2(demultiplexer_2_out4), .out_3(register16_5_out_3));
  Register16 register16_6 (.in_1(demultiplexer_1_out5), .in_2(demultiplexer_2_out5), .out_3(register16_6_out_3));
  Register16 register16_7 (.in_1(demultiplexer_1_out6), .in_2(demultiplexer_2_out6), .out_3(register16_7_out_3));
  Register16 register16_8 (.in_1(demultiplexer_1_out7), .in_2(demultiplexer_2_out7), .out_3(register16_8_out_3));
  Multiplexer #(.select(3), .width(16)) multiplexer_1 (
    .in0(register16_1_out_3), .in1(register16_2_out_3), .in2(register16_3_out_3), .in3(register16_4_out_3),
    .in4(register16_5_out_3), .in5(register16_6_out_3), .in6(register16_7_out_3), .in7(register16_8_out_3),
    .out(out_4), .sel(addr));  // open: en

  // Notes on the sheet:
  //   input
endmodule

module RAM64 (
  input  [15:0] in_1,
  input  [5:0] in_2,
  input  in_3,
  output [15:0] out_4
);

  wire demultiplexer_2_out0, demultiplexer_2_out1, demultiplexer_2_out2, demultiplexer_2_out3,
       demultiplexer_2_out4, demultiplexer_2_out5, demultiplexer_2_out6, demultiplexer_2_out7;
  wire [15:0] demultiplexer_1_out0, demultiplexer_1_out1, demultiplexer_1_out2, demultiplexer_1_out3,
       demultiplexer_1_out4, demultiplexer_1_out5, demultiplexer_1_out6, demultiplexer_1_out7, ram8_1_out_4,
       ram8_2_out_4, ram8_3_out_4, ram8_4_out_4, ram8_5_out_4, ram8_6_out_4, ram8_7_out_4, ram8_8_out_4;

  Demultiplexer #(.select(3), .width(16)) demultiplexer_1 (
    .out0(demultiplexer_1_out0), .out1(demultiplexer_1_out1), .out2(demultiplexer_1_out2),
    .out3(demultiplexer_1_out3), .out4(demultiplexer_1_out4), .out5(demultiplexer_1_out5),
    .out6(demultiplexer_1_out6), .out7(demultiplexer_1_out7), .in(in_1), .sel(in_2[5:3]));  // open: en
  Demultiplexer #(.select(3)) demultiplexer_2 (
    .out0(demultiplexer_2_out0), .out1(demultiplexer_2_out1), .out2(demultiplexer_2_out2),
    .out3(demultiplexer_2_out3), .out4(demultiplexer_2_out4), .out5(demultiplexer_2_out5),
    .out6(demultiplexer_2_out6), .out7(demultiplexer_2_out7), .in(in_3), .sel(in_2[5:3]));  // open: en
  RAM8 ram8_1 (.in_1(demultiplexer_1_out0), .addr(in_2[2:0]), .set(demultiplexer_2_out0), .out_4(ram8_1_out_4));
  RAM8 ram8_2 (.in_1(demultiplexer_1_out1), .addr(in_2[2:0]), .set(demultiplexer_2_out1), .out_4(ram8_2_out_4));
  RAM8 ram8_3 (.in_1(demultiplexer_1_out2), .addr(in_2[2:0]), .set(demultiplexer_2_out2), .out_4(ram8_3_out_4));
  RAM8 ram8_4 (.in_1(demultiplexer_1_out3), .addr(in_2[2:0]), .set(demultiplexer_2_out3), .out_4(ram8_4_out_4));
  RAM8 ram8_5 (.in_1(demultiplexer_1_out4), .addr(in_2[2:0]), .set(demultiplexer_2_out4), .out_4(ram8_5_out_4));
  RAM8 ram8_6 (.in_1(demultiplexer_1_out5), .addr(in_2[2:0]), .set(demultiplexer_2_out5), .out_4(ram8_6_out_4));
  RAM8 ram8_7 (.in_1(demultiplexer_1_out6), .addr(in_2[2:0]), .set(demultiplexer_2_out6), .out_4(ram8_7_out_4));
  RAM8 ram8_8 (.in_1(demultiplexer_1_out7), .addr(in_2[2:0]), .set(demultiplexer_2_out7), .out_4(ram8_8_out_4));
  Multiplexer #(.select(3), .width(16)) multiplexer_1 (
    .in0(ram8_1_out_4), .in1(ram8_2_out_4), .in2(ram8_3_out_4), .in3(ram8_4_out_4), .in4(ram8_5_out_4),
    .in5(ram8_6_out_4), .in6(ram8_7_out_4), .in7(ram8_8_out_4), .out(out_4), .sel(in_2[5:3]));  // open: en
endmodule

module RAM512 (
  input  [15:0] in_1,
  input  [8:0] in_2,
  input  in_3,
  output [15:0] out_4
);

  wire demultiplexer_2_out0, demultiplexer_2_out1, demultiplexer_2_out2, demultiplexer_2_out3,
       demultiplexer_2_out4, demultiplexer_2_out5, demultiplexer_2_out6, demultiplexer_2_out7;
  wire [15:0] demultiplexer_1_out0, demultiplexer_1_out1, demultiplexer_1_out2, demultiplexer_1_out3,
       demultiplexer_1_out4, demultiplexer_1_out5, demultiplexer_1_out6, demultiplexer_1_out7, ram64_1_out_4,
       ram64_2_out_4, ram64_3_out_4, ram64_4_out_4, ram64_5_out_4, ram64_6_out_4, ram64_7_out_4,
       ram64_8_out_4;

  Demultiplexer #(.select(3), .width(16)) demultiplexer_1 (
    .out0(demultiplexer_1_out0), .out1(demultiplexer_1_out1), .out2(demultiplexer_1_out2),
    .out3(demultiplexer_1_out3), .out4(demultiplexer_1_out4), .out5(demultiplexer_1_out5),
    .out6(demultiplexer_1_out6), .out7(demultiplexer_1_out7), .in(in_1), .sel(in_2[8:6]));  // open: en
  Demultiplexer #(.select(3)) demultiplexer_2 (
    .out0(demultiplexer_2_out0), .out1(demultiplexer_2_out1), .out2(demultiplexer_2_out2),
    .out3(demultiplexer_2_out3), .out4(demultiplexer_2_out4), .out5(demultiplexer_2_out5),
    .out6(demultiplexer_2_out6), .out7(demultiplexer_2_out7), .in(in_3), .sel(in_2[8:6]));  // open: en
  RAM64 ram64_1 (.in_1(demultiplexer_1_out0), .in_2(in_2[5:0]), .in_3(demultiplexer_2_out0), .out_4(ram64_1_out_4));
  RAM64 ram64_2 (.in_1(demultiplexer_1_out1), .in_2(in_2[5:0]), .in_3(demultiplexer_2_out1), .out_4(ram64_2_out_4));
  RAM64 ram64_3 (.in_1(demultiplexer_1_out2), .in_2(in_2[5:0]), .in_3(demultiplexer_2_out2), .out_4(ram64_3_out_4));
  RAM64 ram64_4 (.in_1(demultiplexer_1_out3), .in_2(in_2[5:0]), .in_3(demultiplexer_2_out3), .out_4(ram64_4_out_4));
  RAM64 ram64_5 (.in_1(demultiplexer_1_out4), .in_2(in_2[5:0]), .in_3(demultiplexer_2_out4), .out_4(ram64_5_out_4));
  RAM64 ram64_6 (.in_1(demultiplexer_1_out5), .in_2(in_2[5:0]), .in_3(demultiplexer_2_out5), .out_4(ram64_6_out_4));
  RAM64 ram64_7 (.in_1(demultiplexer_1_out6), .in_2(in_2[5:0]), .in_3(demultiplexer_2_out6), .out_4(ram64_7_out_4));
  RAM64 ram64_8 (.in_1(demultiplexer_1_out7), .in_2(in_2[5:0]), .in_3(demultiplexer_2_out7), .out_4(ram64_8_out_4));
  Multiplexer #(.select(3), .width(16)) multiplexer_1 (
    .in0(ram64_1_out_4), .in1(ram64_2_out_4), .in2(ram64_3_out_4), .in3(ram64_4_out_4), .in4(ram64_5_out_4),
    .in5(ram64_6_out_4), .in6(ram64_7_out_4), .in7(ram64_8_out_4), .out(out_4), .sel(in_2[8:6]));  // open: en
endmodule

module RAM4K (
  input  [15:0] in_1,
  input  [8:0] in_2,
  input  in_3,
  output [15:0] out_4
);

  wire demultiplexer_2_out0, demultiplexer_2_out1, demultiplexer_2_out2, demultiplexer_2_out3,
       demultiplexer_2_out4, demultiplexer_2_out5, demultiplexer_2_out6, demultiplexer_2_out7;
  wire [15:0] demultiplexer_1_out0, demultiplexer_1_out1, demultiplexer_1_out2, demultiplexer_1_out3,
       demultiplexer_1_out4, demultiplexer_1_out5, demultiplexer_1_out6, demultiplexer_1_out7, ram64_1_out_4,
       ram64_2_out_4, ram64_3_out_4, ram64_4_out_4, ram64_5_out_4, ram64_6_out_4, ram64_7_out_4,
       ram64_8_out_4;

  Demultiplexer #(.select(3), .width(16)) demultiplexer_1 (
    .out0(demultiplexer_1_out0), .out1(demultiplexer_1_out1), .out2(demultiplexer_1_out2),
    .out3(demultiplexer_1_out3), .out4(demultiplexer_1_out4), .out5(demultiplexer_1_out5),
    .out6(demultiplexer_1_out6), .out7(demultiplexer_1_out7), .in(in_1), .sel(in_2[8:6]));  // open: en
  Demultiplexer #(.select(3)) demultiplexer_2 (
    .out0(demultiplexer_2_out0), .out1(demultiplexer_2_out1), .out2(demultiplexer_2_out2),
    .out3(demultiplexer_2_out3), .out4(demultiplexer_2_out4), .out5(demultiplexer_2_out5),
    .out6(demultiplexer_2_out6), .out7(demultiplexer_2_out7), .in(in_3), .sel(in_2[8:6]));  // open: en
  RAM64 ram64_1 (.in_1(demultiplexer_1_out0), .in_2(in_2[5:0]), .in_3(demultiplexer_2_out0), .out_4(ram64_1_out_4));
  RAM64 ram64_2 (.in_1(demultiplexer_1_out1), .in_2(in_2[5:0]), .in_3(demultiplexer_2_out1), .out_4(ram64_2_out_4));
  RAM64 ram64_3 (.in_1(demultiplexer_1_out2), .in_2(in_2[5:0]), .in_3(demultiplexer_2_out2), .out_4(ram64_3_out_4));
  RAM64 ram64_4 (.in_1(demultiplexer_1_out3), .in_2(in_2[5:0]), .in_3(demultiplexer_2_out3), .out_4(ram64_4_out_4));
  RAM64 ram64_5 (.in_1(demultiplexer_1_out4), .in_2(in_2[5:0]), .in_3(demultiplexer_2_out4), .out_4(ram64_5_out_4));
  RAM64 ram64_6 (.in_1(demultiplexer_1_out5), .in_2(in_2[5:0]), .in_3(demultiplexer_2_out5), .out_4(ram64_6_out_4));
  RAM64 ram64_7 (.in_1(demultiplexer_1_out6), .in_2(in_2[5:0]), .in_3(demultiplexer_2_out6), .out_4(ram64_7_out_4));
  RAM64 ram64_8 (.in_1(demultiplexer_1_out7), .in_2(in_2[5:0]), .in_3(demultiplexer_2_out7), .out_4(ram64_8_out_4));
  Multiplexer #(.select(3), .width(16)) multiplexer_1 (
    .in0(ram64_1_out_4), .in1(ram64_2_out_4), .in2(ram64_3_out_4), .in3(ram64_4_out_4), .in4(ram64_5_out_4),
    .in5(ram64_6_out_4), .in6(ram64_7_out_4), .in7(ram64_8_out_4), .out(out_4), .sel(in_2[8:6]));  // open: en
endmodule

module CPU (
  input  [15:0] instruction,
  input  [15:0] inM,
  input  reset,
  input  in_4,
  output [15:0] outM,
  output writeM,
  output [14:0] addressM,
  output [14:0] pc
);

  wire alu_1_ng, alu_1_zr, and_1_out, and_2_out, and_3_out, nor_1_out, nor_2_out;
  wire [15:0] A_Register_q, alu_1_out_9, D_Register_q, demultiplexer_1_out1, demultiplexer_1_out2,
       demultiplexer_1_out3, demultiplexer_1_out4, demultiplexer_1_out5, demultiplexer_1_out6,
       demultiplexer_1_out7, multiplexer_1_out, multiplexer_3_out, or_1_out, or_2_out;

  assign or_1_out = demultiplexer_1_out4 | demultiplexer_1_out5 | demultiplexer_1_out6 | demultiplexer_1_out7;  // OR_Gate or_1, 16 bits wide
  Multiplexer #(.width(16)) multiplexer_1 (
    .in0(or_1_out), .in1(instruction), .out(multiplexer_1_out), .sel(nor_1_out));  // open: en
  Register #(.width(16)) A_Register (
    .D(multiplexer_1_out), .Q({A_Register_q[15:4], writeM, A_Register_q[2:0]}), .clk(in_4));  // open: en, clr
  Multiplexer #(.width(15)) multiplexer_2 (
    .in0(pc), .in1({A_Register_q[14:4], writeM, A_Register_q[2:0]}), .out(addressM), .sel(A_Register_q[15]));  // open: en
  assign or_2_out = demultiplexer_1_out2 | demultiplexer_1_out3 | demultiplexer_1_out6 | demultiplexer_1_out7;  // OR_Gate or_2, 16 bits wide
  Register #(.width(16)) D_Register (.D(or_2_out), .Q(D_Register_q), .clk(in_4));  // open: en, clr
  Multiplexer #(.width(16)) multiplexer_3 (
    .in0({A_Register_q[15:4], writeM, A_Register_q[2:0]}), .in1(inM), .out(multiplexer_3_out),
    .sel(A_Register_q[12]));  // open: en
  nor nor_1 (nor_1_out, and_1_out, and_2_out, and_3_out);
  Counter #(.width(15), .max('h7fff)) counter_1 (
    .load(reset), .D(addressM), .Q(pc), .clk(in_4));  // open: count, carry, clr
  Demultiplexer #(.select(3), .width(16)) demultiplexer_1 (
    .out1(demultiplexer_1_out1), .out2(demultiplexer_1_out2), .out3(demultiplexer_1_out3),
    .out4(demultiplexer_1_out4), .out5(demultiplexer_1_out5), .out6(demultiplexer_1_out6),
    .out7(demultiplexer_1_out7), .in(alu_1_out_9), .sel({A_Register_q[5:4], writeM}));  // open: out0, en
  ALU alu_1 (
    .x(D_Register_q), .in_8(multiplexer_3_out), .out_9(alu_1_out_9), .zr(alu_1_zr), .ng(alu_1_ng),
    .zx(A_Register_q[11]), .nx(A_Register_q[10]), .zy(A_Register_q[9]), .ny(A_Register_q[8]),
    .f(A_Register_q[7]), .no(A_Register_q[6]));
  and and_1 (and_1_out, A_Register_q[2], alu_1_ng);
  assign outM = demultiplexer_1_out1 | demultiplexer_1_out3 | demultiplexer_1_out5 | demultiplexer_1_out7;  // OR_Gate or_3, 16 bits wide
  and and_2 (and_2_out, A_Register_q[1], alu_1_zr);
  nor nor_2 (nor_2_out, alu_1_ng, alu_1_zr);
  and and_3 (and_3_out, A_Register_q[0], nor_2_out);
endmodule

module Computer (
  input  in_1,
  output [15:0] out_2,
  output [15:0] out_3
);

  wire clock_1_out, cpu_1_writem, not_1_out;
  wire [14:0] cpu_1_addressm, cpu_1_pc;
  wire [15:0] cpu_1_outm;

  Clock clock_1 (.out(clock_1_out));
  ROM #(.addrWidth(15), .dataWidth(16)) rom_1 (.addr(cpu_1_pc), .data(out_2));  // open: sel
  CPU cpu_1 (
    .instruction(out_2), .inM(out_3), .reset(in_1), .outM(cpu_1_outm), .writeM(cpu_1_writem),
    .addressM(cpu_1_addressm), .pc(cpu_1_pc), .in_4(clock_1_out));
  assign out_3 = cpu_1_writem ? cpu_1_outm : 16'bz;  // Controlled_Buffer controlled_buffer_1
  not not_1 (not_1_out, cpu_1_writem);
  RAM #(.addrWidth(15), .dataWidth(16)) ram_1 (
    .addr(cpu_1_addressm), .data(out_3), .clk(clock_1_out), .ld(not_1_out));  // open: sel, clr

  // Notes on the sheet:
  //   ROM
  //   contents of rom_1 (hex, n*v repeats v):
  //   10 efc8 11 ea88 10 fc10 0 f4d0 12 e301 10 fc10 11 f088 10 fdc8 4 ea87 11 fc10
  //   RAM
endmodule

module Cpu_test (
  input  [15:0] in_1,
  input  [15:0] in_2,
  input  in_3,
  input  in_4,
  output [15:0] out_5,
  output out_6,
  output [14:0] out_7,
  output [14:0] out_8
);

  CPU cpu_1 (
    .instruction(in_1), .inM(in_2), .reset(in_3), .outM(out_5), .writeM(out_6), .addressM(out_7), .pc(out_8),
    .in_4(in_4));
endmodule

module computer_1 (
  input  reset,
  output writeM,
  output [14:0] addressM,
  output [14:0] pc
);

  wire alu_1_ng, alu_1_zr, and_1_out, and_2_out, and_3_out, clock_1_out, nor_1_out, nor_2_out, not_1_out;
  wire [14:0] multiplexer_2_out;
  wire [15:0] A_Register_q, alu_1_out_9, controlled_buffer_1_out, D_Register_q, demultiplexer_1_out1,
       demultiplexer_1_out2, demultiplexer_1_out3, demultiplexer_1_out4, demultiplexer_1_out5,
       demultiplexer_1_out6, demultiplexer_1_out7, multiplexer_1_out, multiplexer_3_out, or_1_out, or_2_out,
       or_3_out, rom_1_data;

  Clock clock_1 (.out(clock_1_out));
  ROM #(.addrWidth(15), .dataWidth(16)) rom_1 (.addr(pc), .data(rom_1_data));  // open: sel
  assign or_1_out = demultiplexer_1_out4 | demultiplexer_1_out5 | demultiplexer_1_out6 | demultiplexer_1_out7;  // OR_Gate or_1, 16 bits wide
  Multiplexer #(.width(16)) multiplexer_1 (
    .in0(or_1_out), .in1(rom_1_data), .out(multiplexer_1_out), .sel(nor_1_out));  // open: en
  Register #(.width(16)) A_Register (
    .D(multiplexer_1_out), .Q({A_Register_q[15:4], writeM, A_Register_q[2:0]}), .clk(clock_1_out));  // open: en, clr
  Multiplexer #(.width(15)) multiplexer_2 (
    .in0({A_Register_q[14:4], writeM, A_Register_q[2:0]}), .in1(pc), .out(multiplexer_2_out),
    .sel(A_Register_q[15]));  // open: en
  assign or_2_out = demultiplexer_1_out2 | demultiplexer_1_out3 | demultiplexer_1_out6 | demultiplexer_1_out7;  // OR_Gate or_2, 16 bits wide
  Register #(.width(16)) D_Register (.D(or_2_out), .Q(D_Register_q), .clk(clock_1_out));  // open: en, clr
  Multiplexer #(.width(16)) multiplexer_3 (
    .in0({A_Register_q[15:4], writeM, A_Register_q[2:0]}), .in1(controlled_buffer_1_out),
    .out(multiplexer_3_out), .sel(A_Register_q[12]));  // open: en
  nor nor_1 (nor_1_out, and_1_out, and_2_out, and_3_out);
  Counter #(.width(15), .max('h7fff)) counter_1 (
    .load(reset), .D(multiplexer_2_out), .Q(pc), .clk(clock_1_out));  // open: count, carry, clr
  Demultiplexer #(.select(3), .width(16)) demultiplexer_1 (
    .out1(demultiplexer_1_out1), .out2(demultiplexer_1_out2), .out3(demultiplexer_1_out3),
    .out4(demultiplexer_1_out4), .out5(demultiplexer_1_out5), .out6(demultiplexer_1_out6),
    .out7(demultiplexer_1_out7), .in(alu_1_out_9), .sel({A_Register_q[5:4], writeM}));  // open: out0, en
  ALU alu_1 (
    .x(D_Register_q), .in_8(multiplexer_3_out), .out_9(alu_1_out_9), .zr(alu_1_zr), .ng(alu_1_ng),
    .zx(A_Register_q[11]), .nx(A_Register_q[10]), .zy(A_Register_q[9]), .ny(A_Register_q[8]),
    .f(A_Register_q[7]), .no(A_Register_q[6]));
  and and_1 (and_1_out, A_Register_q[2], alu_1_ng);
  assign or_3_out = demultiplexer_1_out1 | demultiplexer_1_out3 | demultiplexer_1_out5 | demultiplexer_1_out7;  // OR_Gate or_3, 16 bits wide
  and and_2 (and_2_out, A_Register_q[1], alu_1_zr);
  nor nor_2 (nor_2_out, alu_1_ng, alu_1_zr);
  and and_3 (and_3_out, A_Register_q[0], nor_2_out);
  assign controlled_buffer_1_out = writeM ? or_3_out : 16'bz;  // Controlled_Buffer controlled_buffer_1
  Register #(.width(15)) D_Register_2 (.D(multiplexer_2_out), .Q(addressM), .clk(clock_1_out));  // open: en, clr
  not not_1 (not_1_out, writeM);
  RAM #(.addrWidth(15), .dataWidth(16)) ram_1 (
    .addr(addressM), .data(controlled_buffer_1_out), .clk(clock_1_out), .ld(not_1_out));  // open: sel, clr

  // Notes on the sheet:
  //   ROM
  //   contents of rom_1 (hex, n*v repeats v):
  //   10 efc8 11 ea88 10 fc10 0 f4d0 12 e301 10 fc10 11 f088 10 fdc8 4 ea87 11 fc10
  //   RAM
endmodule
